# Fritzing sketch annoying_v1 (saved by Fritzing 0.9.4)
perfboards: 1

parts:
  Mod1 = Raspberry Pi Pico
  SP1 = SPEAKER [package=pcb_mount_speaker]
  IC1 = IC, DIP package, 8 pins [chip_label=IC]
  Q1 = Basic FET P-Channel [package="TO220 [THT]"]
  Q2 = Basic FET N-Channel [package="D2Pak [SMD]"]
  ZS-042_RTC1 = ZS-042 RTC Module
  R1 = Resistor [tolerance=±5% resistance=22k package=THT]
  R2 = Resistor [tolerance=±5% resistance=22k package=THT]
  R3 = Resistor [tolerance=±5% resistance=3k package=THT]
  C1 = Ceramic Capacitor [capacitance=100nF package="100 mil [THT, multilayer]"]  # not connected
  R4 = Resistor [tolerance=±5% resistance=100k package=THT]
  R5 = Resistor [tolerance=±5% resistance=100k package=THT]
  F2 = FUSE [package=fuse_5mm]
  D1 = Rectifier Diode [package="Melf DO-213 AA [SMD]"]
  M1 = RioRand LM2596
  DFRobot_DFPlayer_Mini1 = DFRobot DFPlayer Mini [part_number=DFR0299]
  VCC1 = Battery block 9V
  Bauteil1 = I2C level shifter bidirectional
  Bauteil2 = Soil Moisture Sensor
  R7 = Resistor [tolerance=±5% resistance=4.7k package=THT]  # not connected
  U1 = SWITCH-SPST-2 [package=r_sw_th]  # not connected

nets (from the schematic view):
  N1: Mod1.pin_1, DFRobot_DFPlayer_Mini1.RX
  N2: Mod1.pin_2, DFRobot_DFPlayer_Mini1.TX
  GND: Mod1.pin_3, Mod1.pin_8, Mod1.pin_13, Mod1.pin_18, Mod1.pin_23, Mod1.pin_28, Mod1.pin_33, Mod1.pin_38, Q2.source, ZS-042_RTC1.GND, R2.Pin_1, M1.Pin_4, DFRobot_DFPlayer_Mini1.GND-1, DFRobot_DFPlayer_Mini1.GND-2, Bauteil1.GND, Bauteil2.GND
  N3: Mod1.pin_21, Bauteil1.LV1
  N4: Mod1.pin_22, Bauteil1.LV2
  N5: Mod1.pin_26, Q2.Gate, R2.Pin_0
  N6: Mod1.pin_34, Bauteil2.SIG
  N7: Mod1.pin_36, Bauteil1.LV, Bauteil2.VCC
  N8: Mod1.pin_39, Q1.drain, DFRobot_DFPlayer_Mini1.VCC
  N9: SP1.+, DFRobot_DFPlayer_Mini1.SPK_1
  N10: SP1.-, DFRobot_DFPlayer_Mini1.SPK_2
  N11: IC1.pin1, IC1.pin5, R4.Pin_0
  N12: IC1.pin2, ZS-042_RTC1.SQW, R3.Pin_0
  N13: IC1.pin3, IC1.pin6, R5.Pin_1
  N14: IC1.pin7, Q2.drain, R1.Pin_0
  N15: IC1.pin8, Q1.source, ZS-042_RTC1.VCC, R1.Pin_1, R3.Pin_1, R4.Pin_1, R5.Pin_0, M1.Pin_3, Bauteil1.HV
  N16: ZS-042_RTC1.SDA, Bauteil1.HV1
  N17: ZS-042_RTC1.SCL, Bauteil1.HV2
  N18: F2.1, VCC1.+
  N19: F2.2, D1.cathode, M1.Pin_1
  N20: D1.anode, M1.Pin_2, VCC1.-

custom parts:
  Raspberry Pi Pico: Raspberry Pi Pico. Based around the RP2040 microcontroller the Pico is a low cost microcontroller device bringing Raspberry Pi quality, cost, and easy of use to the microcontroller space. Jan 2021, Split part in to two versions: tht (this one) and SMD. This one will drill holes for a .1 in header in pcb to allow plugging in the module as well as providing pads to solder the module to the top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
