# Fritzing sketch lec2 (saved by Fritzing 0.9.4)
breadboards: 1

parts:
  NAND = IC, DIP package, 8 pins [chip_label=IC]
  R1 = Resistor [tolerance=±5% resistance=100k package=THT]
  R2 = Resistor [tolerance=±5% resistance=500 package=THT]
  R3 = Resistor [tolerance=±5% resistance=500 package=THT]
  R4 = Resistor [tolerance=±5% resistance=100k package=THT]
  LED1 = smd LED [color="Red (633nm)" package="0805 [SMD]"]
  LED2 = smd LED [color="Red (633nm)" package="0805 [SMD]"]
  Mod1 = Raspberry Pi Pico

nets:
  N1: NAND.pin1, NAND.pin5, R1.Pin_0, LED2.cathode
  N2: NAND.pin2, NAND.pin7, NAND.pin8, R1.Pin_1, R2.Pin_1, R3.Pin_1, R4.Pin_1, Mod1.pin_40
  N3: NAND.pin3, NAND.pin6, R4.Pin_0, LED1.cathode
  N4: NAND.pin4, Mod1.pin_13, Mod1.pin_38
  N5: R2.Pin_0, LED2.anode
  N6: R3.Pin_0, LED1.anode

custom parts:
  Raspberry Pi Pico: Raspberry Pi Pico. Based around the RP2040 microcontroller the Pico is a low cost microcontroller device bringing Raspberry Pi quality, cost, and easy of use to the microcontroller space. Jan 2021, Split part in to two versions: tht (this one) and SMD. This one will drill holes for a .1 in header in pcb to allow plugging in the module as well as providing pads to solder the module to the top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
