# Fritzing sketch lec3 (saved by Fritzing 0.9.4)
breadboards: 1

parts:
  Mod1 = Raspberry Pi Pico
  DFRobot_DFPlayer_Mini1 = DFRobot DFPlayer Mini [part_number=DFR0299]
  SP1 = SPEAKER [package=pcb_mount_speaker]
  Bauteil1 = I2C level shifter bidirectional

nets:
  N1: Mod1.pin_1, Bauteil1.LV3
  N2: Mod1.pin_2, Bauteil1.LV4
  N3: Mod1.pin_3, Mod1.pin_8, Mod1.pin_13, Mod1.pin_18, Mod1.pin_23, Mod1.pin_28, Mod1.pin_33, Mod1.pin_38, DFRobot_DFPlayer_Mini1.GND-1, DFRobot_DFPlayer_Mini1.GND-2, Bauteil1.GND
  N4: Mod1.pin_36, Bauteil1.LV
  N5: Mod1.pin_40, DFRobot_DFPlayer_Mini1.VCC, Bauteil1.HV
  N6: DFRobot_DFPlayer_Mini1.RX, Bauteil1.HV3
  N7: DFRobot_DFPlayer_Mini1.TX, Bauteil1.HV4
  N8: DFRobot_DFPlayer_Mini1.SPK_1, SP1.+
  N9: DFRobot_DFPlayer_Mini1.SPK_2, SP1.-

custom parts:
  Raspberry Pi Pico: Raspberry Pi Pico. Based around the RP2040 microcontroller the Pico is a low cost microcontroller device bringing Raspberry Pi quality, cost, and easy of use to the microcontroller space. Jan 2021, Split part in to two versions: tht (this one) and SMD. This one will drill holes for a .1 in header in pcb to allow plugging in the module as well as providing pads to solder the module to the top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
